// Logisim project hw4.circ as structural Verilog: 14 circuits, main circuit main
module main (
  input  reset,
  input  [2:0] tempread1,
  input  [2:0] tempread2,
  input  [5:0] tempimmediate
);

  wire clk, dataWE, doBranch_dobranch, isBranch, isJal, isJr, isJump, isLoad, isValid, not_1_out, not_2_out,
       not_3_out, or_1_out, printOut, readInput, rfWE, rij_1_isr, useImmediate;
  wire [2:0] ALUop, multiplexer_2_out, multiplexer_3_out, Rd, Rs, Rt, Shamt;
  wire [3:0] opcode;
  wire [5:0] insnsplitter_1_immediate;
  wire [6:0] keyboard_1_data;
  wire [11:0] address;
  wire [15:0] alu_1_output, alu_2_output, bit_extender_1_out, bit_extender_2_out, currPC, dataToStore,
       dataToWrite, multiplexer_1_out, multiplexer_4_out, multiplexer_5_out, multiplexer_6_out,
       multiplexer_7_out, multiplexer_8_out, multiplexer_9_out, n16bitadder_1_output, plus_1_output,
       ram_1_data, rom_1_data, Rsjr;

  Clock u_clk (.out(clk));
  // Probe on multiplexer_9_out
  Multiplexer #(.width(16), .enable("false")) multiplexer_1 (
    .in0(multiplexer_9_out), .in1(Rsjr), .out(multiplexer_1_out), .sel(isJr));
  register PC (.\input (multiplexer_1_out), .clk(clk), .Write_Enable(1'b1), .reset(reset), .out(currPC));
  // Probe on currPC
  ALU plus_1 (.in1a(currPC), .in2b(16'h1), .operation(3'b000), .\output (plus_1_output));  // open: Zero, Overflow
  // Probe on plus_1_output
  ROM #(.addrWidth(16), .dataWidth(16)) rom_1 (.addr(currPC), .data(rom_1_data));  // open: sel
  // Probe on rom_1_data
  RIJ rij_1 (.opcode(opcode), .isR(rij_1_isr));  // open: isI, isJ
  or or_1 (or_1_out, rij_1_isr, readInput);
  ALU alu_1 (.in1a(16'h1), .in2b(currPC), .operation(3'b000), .\output (alu_1_output));  // open: Zero, Overflow
  Multiplexer #(.width(3), .enable("false")) multiplexer_2 (
    .in0(Rt), .in1(Rd), .out(multiplexer_2_out), .sel(or_1_out));
  // Probe on opcode
  not not_1 (not_1_out, clk);
  Multiplexer #(.width(3), .enable("false")) multiplexer_3 (
    .in0(multiplexer_2_out), .in1(3'b111), .out(multiplexer_3_out), .sel(isJal));
  insnSplitter insnsplitter_1 (
    .insn(rom_1_data), .opcode(opcode), .immediate(insnsplitter_1_immediate), .Shamt(Shamt), .Rd(Rd),
    .Rt(Rt), .Rs(Rs), .address(address));
  Multiplexer #(.width(16), .enable("false")) multiplexer_4 (
    .in0(multiplexer_8_out), .in1(alu_1_output), .out(multiplexer_4_out), .sel(isJal));
  controlBox controlbox_1 (
    .opcode(opcode), .dataWE(dataWE), .RfWe(rfWE), .isLoad(isLoad), .useImmediate(useImmediate),
    .ALU2(ALUop[2]), .ALU1(ALUop[1]), .ALU0(ALUop[0]), .isBranch(isBranch), .isJump(isJump), .isJal(isJal),
    .isJr(isJr), .readInput(readInput), .printOutput(printOut));
  RegisterFile RegisterFile (
    .reset(reset), .valToWrite(multiplexer_5_out), .clk(not_1_out), .WE(rfWE), .writeReg(multiplexer_3_out),
    .read1(Rs), .read2(Rt), .ReadData1(Rsjr), .ReadData2(dataToStore));
  Multiplexer #(.width(16), .enable("false")) multiplexer_5 (
    .in0(multiplexer_4_out), .in1(dataToWrite), .out(multiplexer_5_out), .sel(readInput));
  // Probe on dataToStore
  assign bit_extender_1_out = {{10{insnsplitter_1_immediate[5]}}, insnsplitter_1_immediate};  // Bit_Extender bit_extender_1
  Multiplexer #(.width(16), .enable("false")) multiplexer_6 (
    .in0(dataToStore), .in1(bit_extender_1_out), .out(multiplexer_6_out), .sel(useImmediate));
  // Probe on Rsjr
  // Probe on multiplexer_6_out
  // Probe on bit_extender_1_out
  ALU alu_2 (
    .in1a(Rsjr), .in2b(multiplexer_6_out), .operation(ALUop), .\output (alu_2_output));  // open: Zero, Overflow
  // Probe on bit_extender_1_out
  // Probe on alu_2_output
  // Probe on ALUop
  not not_2 (not_2_out, clk);
  _16bitAdder u_16bitadder_1 (
    ._1a(plus_1_output), ._2b(bit_extender_1_out), .\output (n16bitadder_1_output));  // open: overflow
  RAM #(.addrWidth(16), .dataWidth(16), .bus("separate")) ram_1 (
    .addr(alu_2_output), .din(dataToStore), .data(ram_1_data), .str(dataWE), .clk(not_3_out));  // open: sel, ld, clr
  not not_3 (not_3_out, clk);
  Keyboard keyboard_1 (.clk(clk), .re(readInput), .clr(reset), .avail(isValid), .data(keyboard_1_data));
  brancher doBranch (.ALUresult(alu_2_output), .opcode(opcode), .doBranch(doBranch_dobranch));
  Multiplexer #(.width(16), .enable("false")) multiplexer_7 (
    .in0(plus_1_output), .in1(n16bitadder_1_output), .out(multiplexer_7_out), .sel(doBranch_dobranch));
  TTY #(.rows(13), .cols(80)) tty_1 (.data(Rsjr[6:0]), .clk(not_2_out), .we(printOut), .clr(reset));
  Multiplexer #(.width(16), .enable("false")) multiplexer_8 (
    .in0(alu_2_output), .in1(ram_1_data), .out(multiplexer_8_out), .sel(isLoad));
  Multiplexer #(.width(16), .enable("false")) multiplexer_9 (
    .in0(multiplexer_7_out), .in1(bit_extender_2_out), .out(multiplexer_9_out), .sel(isJump));
  assign bit_extender_2_out = {{4{address[11]}}, address};  // Bit_Extender bit_extender_2
  Multiplexer #(.width(16), .enable("false")) multiplexer_10 (
    .in0(16'h80), .in1({{9{1'b0}}, keyboard_1_data}), .out(dataToWrite), .sel(isValid));

  // Notes on the sheet:
  //   Address of instruction in memory that we will execute
  //   Address in, literal instruction out
  //   +4 in MIPS: bc byte-addressed
  //   +1 in ours: word-addressed
  //   contents of rom_1 (hex, n*v repeats v):
  //   6100 6903 2805 f008 62a0 e400 693f b002 203f
  //   Instruction
  //   Each addy in our memory is one word
  //   toWrite reg
  //   fix jump
  //   val1
  //   val2
  //   immediate
  //   result
  //   Choose immediate or register value
  //   00 = reg
  //   01 = imm
  //   000 add
  //   001 sub
  //   010 not
  //   011 xor
  //   100 shift left
  //   101 shift right
  //   no branch.
  //   branch.
  //   branch or na
  //   isValid
endmodule

module register (
  input  [15:0] \input ,
  input  clk,
  input  Write_Enable,
  input  reset,
  output [15:0] out
);

  D_Flip_Flop d_ff_1 (.clk(clk), .D(\input [0]), .Q(out[0]), .en(Write_Enable), .reset(reset));  // open: Qn, preset
  D_Flip_Flop d_ff_2 (.clk(clk), .D(\input [1]), .Q(out[1]), .en(Write_Enable), .reset(reset));  // open: Qn, preset
  D_Flip_Flop d_ff_3 (.clk(clk), .D(\input [2]), .Q(out[2]), .en(Write_Enable), .reset(reset));  // open: Qn, preset
  D_Flip_Flop d_ff_4 (.clk(clk), .D(\input [3]), .Q(out[3]), .en(Write_Enable), .reset(reset));  // open: Qn, preset
  D_Flip_Flop d_ff_5 (.clk(clk), .D(\input [4]), .Q(out[4]), .en(Write_Enable), .reset(reset));  // open: Qn, preset
  D_Flip_Flop d_ff_6 (.clk(clk), .D(\input [5]), .Q(out[5]), .en(Write_Enable), .reset(reset));  // open: Qn, preset
  D_Flip_Flop d_ff_7 (.clk(clk), .D(\input [6]), .Q(out[6]), .en(Write_Enable), .reset(reset));  // open: Qn, preset
  D_Flip_Flop d_ff_8 (.clk(clk), .D(\input [7]), .Q(out[7]), .en(Write_Enable), .reset(reset));  // open: Qn, preset
  D_Flip_Flop d_ff_9 (.clk(clk), .D(\input [8]), .Q(out[8]), .en(Write_Enable), .reset(reset));  // open: Qn, preset
  D_Flip_Flop d_ff_10 (.clk(clk), .D(\input [9]), .Q(out[9]), .en(Write_Enable), .reset(reset));  // open: Qn, preset
  D_Flip_Flop d_ff_11 (.clk(clk), .D(\input [10]), .Q(out[10]), .en(Write_Enable), .reset(reset));  // open: Qn, preset
  D_Flip_Flop d_ff_12 (.clk(clk), .D(\input [11]), .Q(out[11]), .en(Write_Enable), .reset(reset));  // open: Qn, preset
  D_Flip_Flop d_ff_13 (.clk(clk), .D(\input [12]), .Q(out[12]), .en(Write_Enable), .reset(reset));  // open: Qn, preset
  D_Flip_Flop d_ff_14 (.clk(clk), .D(\input [13]), .Q(out[13]), .en(Write_Enable), .reset(reset));  // open: Qn, preset
  D_Flip_Flop d_ff_15 (.clk(clk), .D(\input [14]), .Q(out[14]), .en(Write_Enable), .reset(reset));  // open: Qn, preset
  D_Flip_Flop d_ff_16 (.clk(clk), .D(\input [15]), .Q(out[15]), .en(Write_Enable), .reset(reset));  // open: Qn, preset

  // Other names for the same wires on the sheet: clock = clk; _0o = out[0]; _1o = out[1]; _2o = out[2]; _3o = out[3];
  //   _4o = out[4]; _5o = out[5]; _6o = out[6]; _7o = out[7]; _8o = out[8]; _9o = out[9]; _10o = out[10];
  //   _11o = out[11]; _12o = out[12]; _13o = out[13]; _14o = out[14]; _15o = out[15]; WE = Write_Enable

  // Notes on the sheet:
  //   will set D-FF to 0
endmodule

module RegisterFile (
  input  reset,
  input  [15:0] valToWrite,
  input  clk,
  input  WE,
  input  [2:0] writeReg,
  input  [2:0] read1,
  input  [2:0] read2,
  output [15:0] ReadData1,
  output [15:0] ReadData2
);

  wire and_1_out, and_2_out, and_3_out, and_4_out, and_5_out, and_6_out, and_7_out, decoder_1_out1,
       decoder_1_out2, decoder_1_out3, decoder_1_out4, decoder_1_out5, decoder_1_out6, decoder_1_out7;
  wire [15:0] reg0out, reg1out, reg2out, reg3out, reg4out, reg5out, reg6out, reg7out;

  Decoder #(.select(3)) decoder_1 (
    .out1(decoder_1_out1), .out2(decoder_1_out2), .out3(decoder_1_out3), .out4(decoder_1_out4),
    .out5(decoder_1_out5), .out6(decoder_1_out6), .out7(decoder_1_out7), .sel(writeReg));  // open: out0, en
  and and_1 (and_1_out, decoder_1_out1, WE);
  and and_2 (and_2_out, decoder_1_out2, WE);
  and and_3 (and_3_out, decoder_1_out3, WE);
  register register_1 (.\input (valToWrite), .clk(clk), .Write_Enable(1'b0), .reset(reset), .out(reg0out));
  register register_2 (.\input (valToWrite), .clk(clk), .Write_Enable(and_1_out), .reset(reset), .out(reg1out));
  register register_3 (.\input (valToWrite), .clk(clk), .Write_Enable(and_2_out), .reset(reset), .out(reg2out));
  register register_4 (.\input (valToWrite), .clk(clk), .Write_Enable(and_3_out), .reset(reset), .out(reg3out));
  // Probe on reg0out
  // Probe on reg1out
  // Probe on reg2out
  // Probe on reg3out
  and and_4 (and_4_out, decoder_1_out4, WE);
  and and_5 (and_5_out, decoder_1_out5, WE);
  and and_6 (and_6_out, decoder_1_out6, WE);
  and and_7 (and_7_out, decoder_1_out7, WE);
  register register_5 (.\input (valToWrite), .clk(clk), .Write_Enable(and_4_out), .reset(reset), .out(reg4out));
  register register_6 (.\input (valToWrite), .clk(clk), .Write_Enable(and_5_out), .reset(reset), .out(reg5out));
  register register_7 (.\input (valToWrite), .clk(clk), .Write_Enable(and_6_out), .reset(reset), .out(reg6out));
  register register_8 (.\input (valToWrite), .clk(clk), .Write_Enable(and_7_out), .reset(reset), .out(reg7out));
  // Probe on reg4out
  // Probe on reg5out
  // Probe on reg6out
  // Probe on reg7out
  Multiplexer #(.select(3), .width(16), .enable("false")) multiplexer_1 (
    .in0(reg0out), .in1(reg1out), .in2(reg2out), .in3(reg3out), .in4(reg4out), .in5(reg5out), .in6(reg6out),
    .in7(reg7out), .out(ReadData2), .sel(read2));
  // Probe on read2
  Multiplexer #(.select(3), .width(16), .enable("false")) multiplexer_2 (
    .in0(reg0out), .in1(reg1out), .in2(reg2out), .in3(reg3out), .in4(reg4out), .in5(reg5out), .in6(reg6out),
    .in7(reg7out), .out(ReadData1), .sel(read1));
  // Probe on read1

  // Other names for the same wires on the sheet: readSource1[2:0] = read1; readSource2[2:0] = read2

  // Notes on the sheet:
  //   RD / destination register
  //   source register 1
  //   source register 2
  //   Value to write if WE is high
  //   Get Val in Reg Source 2
  //   Get Val in Reg Source 1
endmodule

// +
module ALU (
  input  [15:0] in1a,
  input  [15:0] in2b,
  input  [2:0] operation,
  output Zero,
  output Overflow,
  output [15:0] \output 
);

  wire [15:0] leftshifter_1_output, n16bitadder_1_output, Not_out, rightshifter_1_out, subtractor_1_out,
       xor_1_out;

  _16bitAdder u_16bitadder_1 (._1a(in1a), ._2b(in2b), .overflow(Overflow), .\output (n16bitadder_1_output));
  assign Not_out = ~in1a;  // NOT_Gate Not, 16 bits wide
  assign xor_1_out = in1a ^ in2b;  // XOR_Gate xor_1, 16 bits wide
  subtractor subtractor_1 (._1a(in1a), ._2b(in2b), .out(subtractor_1_out));
  leftShifter leftshifter_1 (.\input (in1a), .amount(in2b[2:0]), .\output (leftshifter_1_output));
  rightShifter rightshifter_1 (.\input (in1a), .amount(in2b[2:0]), .out(rightshifter_1_out));
  Multiplexer #(.select(3), .width(16), .enable("false")) multiplexer_1 (
    .in0(n16bitadder_1_output), .in1(subtractor_1_out), .in2(Not_out), .in3(xor_1_out),
    .in4(leftshifter_1_output), .in5(rightshifter_1_out), .out(\output ), .sel(operation));  // open: in6, in7
  isZero iszero_1 (.\input (\output ), .out(Zero));

  // Notes on the sheet:
  //   rs
  //   Get amount from same place as immediate
endmodule

module full_adder (
  input  Cin,
  input  a,
  input  b,
  output s,
  output cout
);

  wire and_1_out, and_2_out, xor_1_out;

  and and_1 (and_1_out, a, b);
  and and_2 (and_2_out, Cin, xor_1_out);
  xor xor_1 (xor_1_out, a, b);
  or or_1 (cout, and_2_out, and_1_out);
  xor xor_2 (s, Cin, xor_1_out);
endmodule

module isZero (
  input  [15:0] \input ,
  output out
);

  wire [15:0] not_1_out;

  assign not_1_out = ~\input ;  // NOT_Gate not_1, 16 bits wide
  and and_1 (out, not_1_out[0], not_1_out[1], not_1_out[2], not_1_out[3], not_1_out[4], not_1_out[5], not_1_out[6], not_1_out[7], not_1_out[9], not_1_out[10], not_1_out[11], not_1_out[12], not_1_out[13], not_1_out[14], not_1_out[15]);
endmodule

module _16bitAdder (
  input  [15:0] _1a,
  input  [15:0] _2b,
  output overflow,
  output [15:0] \output 
);

  wire _0_cout, _1_cout, _2_cout, _3_cout, _4_cout, _5_cout, _6_cout, _7_cout, _8_cout, _9_cout, _10_cout,
       _11_cout, _12_cout, _13_cout, _14_cout;

  full_adder _0 (.Cin(1'b0), .a(_1a[0]), .b(_2b[0]), .s(\output [0]), .cout(_0_cout));
  full_adder _1 (.Cin(_0_cout), .a(_1a[1]), .b(_2b[1]), .s(\output [1]), .cout(_1_cout));
  full_adder _2 (.Cin(_1_cout), .a(_1a[2]), .b(_2b[2]), .s(\output [2]), .cout(_2_cout));
  full_adder _3 (.Cin(_2_cout), .a(_1a[3]), .b(_2b[3]), .s(\output [3]), .cout(_3_cout));
  full_adder _4 (.Cin(_3_cout), .a(_1a[4]), .b(_2b[4]), .s(\output [4]), .cout(_4_cout));
  full_adder _5 (.Cin(_4_cout), .a(_1a[5]), .b(_2b[5]), .s(\output [5]), .cout(_5_cout));
  full_adder _6 (.Cin(_5_cout), .a(_1a[6]), .b(_2b[6]), .s(\output [6]), .cout(_6_cout));
  full_adder _7 (.Cin(_6_cout), .a(_1a[7]), .b(_2b[7]), .s(\output [7]), .cout(_7_cout));
  full_adder _8 (.Cin(_7_cout), .a(_1a[8]), .b(_2b[8]), .s(\output [8]), .cout(_8_cout));
  full_adder _9 (.Cin(_8_cout), .a(_1a[9]), .b(_2b[9]), .s(\output [9]), .cout(_9_cout));
  full_adder _10 (.Cin(_9_cout), .a(_1a[10]), .b(_2b[10]), .s(\output [10]), .cout(_10_cout));
  full_adder _11 (.Cin(_10_cout), .a(_1a[11]), .b(_2b[11]), .s(\output [11]), .cout(_11_cout));
  full_adder _12 (.Cin(_11_cout), .a(_1a[12]), .b(_2b[12]), .s(\output [12]), .cout(_12_cout));
  full_adder _13 (.Cin(_12_cout), .a(_1a[13]), .b(_2b[13]), .s(\output [13]), .cout(_13_cout));
  full_adder _14 (.Cin(_13_cout), .a(_1a[14]), .b(_2b[14]), .s(\output [14]), .cout(_14_cout));
  full_adder _15 (.Cin(_14_cout), .a(_1a[15]), .b(_2b[15]), .s(\output [15]), .cout(overflow));
endmodule

module subtractor (
  input  [15:0] _1a,
  input  [15:0] _2b,
  output [15:0] out
);

  wire [15:0] n16bitadder_1_output, not_1_out;

  assign not_1_out = ~_2b;  // NOT_Gate not_1, 16 bits wide
  _16bitAdder u_16bitadder_1 (._1a(_1a), ._2b(not_1_out), .\output (n16bitadder_1_output));  // open: overflow
  _16bitAdder u_16bitadder_2 (._1a(n16bitadder_1_output), ._2b(16'h1), .\output (out));  // open: overflow
endmodule

module leftShifter (
  input  [15:0] \input ,
  input  [2:0] amount,
  output [15:0] \output 
);

  wire multiplexer_1_out, multiplexer_2_out, multiplexer_3_out, multiplexer_4_out, multiplexer_5_out,
       multiplexer_6_out, multiplexer_7_out, multiplexer_8_out, multiplexer_9_out, multiplexer_10_out,
       multiplexer_11_out, multiplexer_12_out, multiplexer_13_out, multiplexer_14_out, multiplexer_15_out,
       multiplexer_16_out, multiplexer_17_out, multiplexer_18_out, multiplexer_19_out, multiplexer_20_out,
       multiplexer_21_out, multiplexer_22_out, multiplexer_23_out, multiplexer_24_out, multiplexer_26_out,
       multiplexer_27_out, multiplexer_30_out, multiplexer_34_out, multiplexer_35_out, multiplexer_39_out,
       multiplexer_40_out, multiplexer_43_out;

  Multiplexer #(.enable("false")) multiplexer_1 (
    .in0(\input [15]), .in1(\input [14]), .out(multiplexer_1_out), .sel(amount[0]));
  Multiplexer #(.enable("false")) multiplexer_2 (
    .in0(\input [14]), .in1(\input [13]), .out(multiplexer_2_out), .sel(amount[0]));
  Multiplexer #(.enable("false")) multiplexer_3 (
    .in0(\input [13]), .in1(\input [12]), .out(multiplexer_3_out), .sel(amount[0]));
  Multiplexer #(.enable("false")) multiplexer_4 (
    .in0(\input [12]), .in1(\input [11]), .out(multiplexer_4_out), .sel(amount[0]));
  Multiplexer #(.enable("false")) multiplexer_5 (
    .in0(\input [11]), .in1(\input [10]), .out(multiplexer_5_out), .sel(amount[0]));
  Multiplexer #(.enable("false")) multiplexer_6 (
    .in0(\input [10]), .in1(\input [9]), .out(multiplexer_6_out), .sel(amount[0]));
  Multiplexer #(.enable("false")) multiplexer_7 (
    .in0(\input [9]), .in1(\input [8]), .out(multiplexer_7_out), .sel(amount[0]));
  Multiplexer #(.enable("false")) multiplexer_8 (
    .in0(\input [8]), .in1(\input [7]), .out(multiplexer_8_out), .sel(amount[0]));
  Multiplexer #(.enable("false")) multiplexer_9 (
    .in0(\input [7]), .in1(\input [6]), .out(multiplexer_9_out), .sel(amount[0]));
  Multiplexer #(.enable("false")) multiplexer_10 (
    .in0(\input [6]), .in1(\input [5]), .out(multiplexer_10_out), .sel(amount[0]));
  Multiplexer #(.enable("false")) multiplexer_11 (
    .in0(\input [5]), .in1(\input [4]), .out(multiplexer_11_out), .sel(amount[0]));
  Multiplexer #(.enable("false")) multiplexer_12 (
    .in0(\input [4]), .in1(\input [3]), .out(multiplexer_12_out), .sel(amount[0]));
  Multiplexer #(.enable("false")) multiplexer_13 (
    .in0(\input [3]), .in1(\input [2]), .out(multiplexer_13_out), .sel(amount[0]));
  Multiplexer #(.enable("false")) multiplexer_14 (
    .in0(\input [2]), .in1(\input [1]), .out(multiplexer_14_out), .sel(amount[0]));
  Multiplexer #(.enable("false")) multiplexer_15 (
    .in0(\input [1]), .in1(\input [0]), .out(multiplexer_15_out), .sel(amount[0]));
  Multiplexer #(.enable("false")) multiplexer_16 (
    .in0(\input [0]), .in1(1'b0), .out(multiplexer_16_out), .sel(amount[0]));
  Multiplexer #(.enable("false")) multiplexer_17 (
    .in0(multiplexer_1_out), .in1(multiplexer_3_out), .out(multiplexer_17_out), .sel(amount[1]));
  Multiplexer #(.enable("false")) multiplexer_18 (
    .in0(multiplexer_2_out), .in1(multiplexer_4_out), .out(multiplexer_18_out), .sel(amount[1]));
  Multiplexer #(.enable("false")) multiplexer_19 (
    .in0(multiplexer_3_out), .in1(multiplexer_5_out), .out(multiplexer_19_out), .sel(amount[1]));
  Multiplexer #(.enable("false")) multiplexer_20 (
    .in0(multiplexer_4_out), .in1(multiplexer_6_out), .out(multiplexer_20_out), .sel(amount[1]));
  Multiplexer #(.enable("false")) multiplexer_21 (
    .in0(multiplexer_5_out), .in1(multiplexer_7_out), .out(multiplexer_21_out), .sel(amount[1]));
  Multiplexer #(.enable("false")) multiplexer_22 (
    .in0(multiplexer_6_out), .in1(multiplexer_8_out), .out(multiplexer_22_out), .sel(amount[1]));
  Multiplexer #(.enable("false")) multiplexer_23 (
    .in0(multiplexer_7_out), .in1(multiplexer_9_out), .out(multiplexer_23_out), .sel(amount[1]));
  Multiplexer #(.enable("false")) multiplexer_24 (
    .in0(multiplexer_8_out), .in1(multiplexer_10_out), .out(multiplexer_24_out), .sel(amount[1]));
  Multiplexer #(.enable("false")) multiplexer_25 (
    .in0(multiplexer_17_out), .in1(multiplexer_21_out), .out(\output [15]), .sel(amount[2]));
  Multiplexer #(.enable("false")) multiplexer_26 (
    .in0(multiplexer_9_out), .in1(multiplexer_11_out), .out(multiplexer_26_out), .sel(amount[1]));
  Multiplexer #(.enable("false")) multiplexer_27 (
    .in0(multiplexer_10_out), .in1(multiplexer_12_out), .out(multiplexer_27_out), .sel(amount[1]));
  Multiplexer #(.enable("false")) multiplexer_28 (
    .in0(multiplexer_18_out), .in1(multiplexer_22_out), .out(\output [14]), .sel(amount[2]));
  Multiplexer #(.enable("false")) multiplexer_29 (
    .in0(multiplexer_19_out), .in1(multiplexer_23_out), .out(\output [13]), .sel(amount[2]));
  Multiplexer #(.enable("false")) multiplexer_30 (
    .in0(multiplexer_11_out), .in1(multiplexer_13_out), .out(multiplexer_30_out), .sel(amount[1]));
  Multiplexer #(.enable("false")) multiplexer_31 (
    .in0(multiplexer_20_out), .in1(multiplexer_24_out), .out(\output [12]), .sel(amount[2]));
  Multiplexer #(.enable("false")) multiplexer_32 (
    .in0(multiplexer_21_out), .in1(multiplexer_26_out), .out(\output [11]), .sel(amount[2]));
  Multiplexer #(.enable("false")) multiplexer_33 (
    .in0(multiplexer_22_out), .in1(multiplexer_27_out), .out(\output [10]), .sel(amount[2]));
  Multiplexer #(.enable("false")) multiplexer_34 (
    .in0(multiplexer_12_out), .in1(multiplexer_14_out), .out(multiplexer_34_out), .sel(amount[1]));
  Multiplexer #(.enable("false")) multiplexer_35 (
    .in0(multiplexer_13_out), .in1(multiplexer_15_out), .out(multiplexer_35_out), .sel(amount[1]));
  Multiplexer #(.enable("false")) multiplexer_36 (
    .in0(multiplexer_23_out), .in1(multiplexer_30_out), .out(\output [9]), .sel(amount[2]));
  Multiplexer #(.enable("false")) multiplexer_37 (
    .in0(multiplexer_24_out), .in1(multiplexer_34_out), .out(\output [8]), .sel(amount[2]));
  Multiplexer #(.enable("false")) multiplexer_38 (
    .in0(multiplexer_26_out), .in1(multiplexer_35_out), .out(\output [7]), .sel(amount[2]));
  Multiplexer #(.enable("false")) multiplexer_39 (
    .in0(multiplexer_14_out), .in1(multiplexer_16_out), .out(multiplexer_39_out), .sel(amount[1]));
  Multiplexer #(.enable("false")) multiplexer_40 (
    .in0(multiplexer_15_out), .in1(1'b0), .out(multiplexer_40_out), .sel(amount[1]));
  Multiplexer #(.enable("false")) multiplexer_41 (
    .in0(multiplexer_27_out), .in1(multiplexer_39_out), .out(\output [6]), .sel(amount[2]));
  Multiplexer #(.enable("false")) multiplexer_42 (
    .in0(multiplexer_30_out), .in1(multiplexer_40_out), .out(\output [5]), .sel(amount[2]));
  Multiplexer #(.enable("false")) multiplexer_43 (
    .in0(multiplexer_16_out), .in1(1'b0), .out(multiplexer_43_out), .sel(amount[1]));
  Multiplexer #(.enable("false")) multiplexer_44 (
    .in0(multiplexer_34_out), .in1(multiplexer_43_out), .out(\output [4]), .sel(amount[2]));
  Multiplexer #(.enable("false")) multiplexer_45 (
    .in0(multiplexer_35_out), .in1(1'b0), .out(\output [3]), .sel(amount[2]));
  Multiplexer #(.enable("false")) multiplexer_46 (
    .in0(multiplexer_39_out), .in1(1'b0), .out(\output [2]), .sel(amount[2]));
  Multiplexer #(.enable("false")) multiplexer_47 (
    .in0(multiplexer_40_out), .in1(1'b0), .out(\output [1]), .sel(amount[2]));
  Multiplexer #(.enable("false")) multiplexer_48 (
    .in0(multiplexer_43_out), .in1(1'b0), .out(\output [0]), .sel(amount[2]));

  // Other names for the same wires on the sheet: a0 = amount[0]; a1 = amount[1]; a2 = amount[2]

  // Notes on the sheet:
  //   15
  //   3
  //   2
  //   1
  //   0
  //   14
  //   7
  //   6
  //   5
  //   4
  //   13
  //   12
  //   8
  //   11
  //   9
  //   10
  //   15, 14
  //   11,10
  //   7,6
  //   0
  //   out15
  //   out14
endmodule

module rightShifter (
  input  [15:0] \input ,
  input  [2:0] amount,
  output [15:0] out
);

  wire multiplexer_1_out, multiplexer_2_out, multiplexer_3_out, multiplexer_4_out, multiplexer_5_out,
       multiplexer_6_out, multiplexer_7_out, multiplexer_8_out, multiplexer_9_out, multiplexer_10_out,
       multiplexer_11_out, multiplexer_12_out, multiplexer_13_out, multiplexer_14_out, multiplexer_15_out,
       multiplexer_16_out, multiplexer_17_out, multiplexer_18_out, multiplexer_19_out, multiplexer_20_out,
       multiplexer_21_out, multiplexer_22_out, multiplexer_23_out, multiplexer_24_out, multiplexer_26_out,
       multiplexer_27_out, multiplexer_30_out, multiplexer_34_out, multiplexer_35_out, multiplexer_39_out,
       multiplexer_40_out, multiplexer_43_out;

  Multiplexer #(.enable("false")) multiplexer_1 (
    .in0(\input [0]), .in1(\input [1]), .out(multiplexer_1_out), .sel(amount[0]));
  Multiplexer #(.enable("false")) multiplexer_2 (
    .in0(\input [1]), .in1(\input [2]), .out(multiplexer_2_out), .sel(amount[0]));
  Multiplexer #(.enable("false")) multiplexer_3 (
    .in0(\input [2]), .in1(\input [3]), .out(multiplexer_3_out), .sel(amount[0]));
  Multiplexer #(.enable("false")) multiplexer_4 (
    .in0(\input [3]), .in1(\input [4]), .out(multiplexer_4_out), .sel(amount[0]));
  Multiplexer #(.enable("false")) multiplexer_5 (
    .in0(\input [4]), .in1(\input [5]), .out(multiplexer_5_out), .sel(amount[0]));
  Multiplexer #(.enable("false")) multiplexer_6 (
    .in0(\input [5]), .in1(\input [6]), .out(multiplexer_6_out), .sel(amount[0]));
  Multiplexer #(.enable("false")) multiplexer_7 (
    .in0(\input [6]), .in1(\input [7]), .out(multiplexer_7_out), .sel(amount[0]));
  Multiplexer #(.enable("false")) multiplexer_8 (
    .in0(\input [7]), .in1(\input [8]), .out(multiplexer_8_out), .sel(amount[0]));
  Multiplexer #(.enable("false")) multiplexer_9 (
    .in0(\input [8]), .in1(\input [9]), .out(multiplexer_9_out), .sel(amount[0]));
  Multiplexer #(.enable("false")) multiplexer_10 (
    .in0(\input [9]), .in1(\input [10]), .out(multiplexer_10_out), .sel(amount[0]));
  Multiplexer #(.enable("false")) multiplexer_11 (
    .in0(\input [10]), .in1(\input [11]), .out(multiplexer_11_out), .sel(amount[0]));
  Multiplexer #(.enable("false")) multiplexer_12 (
    .in0(\input [11]), .in1(\input [12]), .out(multiplexer_12_out), .sel(amount[0]));
  Multiplexer #(.enable("false")) multiplexer_13 (
    .in0(\input [12]), .in1(\input [13]), .out(multiplexer_13_out), .sel(amount[0]));
  Multiplexer #(.enable("false")) multiplexer_14 (
    .in0(\input [12]), .in1(\input [14]), .out(multiplexer_14_out), .sel(amount[0]));
  Multiplexer #(.enable("false")) multiplexer_15 (
    .in0(\input [12]), .in1(\input [15]), .out(multiplexer_15_out), .sel(amount[0]));
  Multiplexer #(.enable("false")) multiplexer_16 (
    .in0(\input [15]), .in1(\input [15]), .out(multiplexer_16_out), .sel(amount[0]));
  Multiplexer #(.enable("false")) multiplexer_17 (
    .in0(multiplexer_1_out), .in1(multiplexer_3_out), .out(multiplexer_17_out), .sel(amount[1]));
  Multiplexer #(.enable("false")) multiplexer_18 (
    .in0(multiplexer_2_out), .in1(multiplexer_4_out), .out(multiplexer_18_out), .sel(amount[1]));
  Multiplexer #(.enable("false")) multiplexer_19 (
    .in0(multiplexer_3_out), .in1(multiplexer_5_out), .out(multiplexer_19_out), .sel(amount[1]));
  Multiplexer #(.enable("false")) multiplexer_20 (
    .in0(multiplexer_4_out), .in1(multiplexer_6_out), .out(multiplexer_20_out), .sel(amount[1]));
  Multiplexer #(.enable("false")) multiplexer_21 (
    .in0(multiplexer_5_out), .in1(multiplexer_7_out), .out(multiplexer_21_out), .sel(amount[1]));
  Multiplexer #(.enable("false")) multiplexer_22 (
    .in0(multiplexer_6_out), .in1(multiplexer_8_out), .out(multiplexer_22_out), .sel(amount[1]));
  Multiplexer #(.enable("false")) multiplexer_23 (
    .in0(multiplexer_7_out), .in1(multiplexer_9_out), .out(multiplexer_23_out), .sel(amount[1]));
  Multiplexer #(.enable("false")) multiplexer_24 (
    .in0(multiplexer_8_out), .in1(multiplexer_10_out), .out(multiplexer_24_out), .sel(amount[1]));
  Multiplexer #(.enable("false")) multiplexer_25 (
    .in0(multiplexer_17_out), .in1(multiplexer_21_out), .out(out[0]), .sel(amount[2]));
  Multiplexer #(.enable("false")) multiplexer_26 (
    .in0(multiplexer_9_out), .in1(multiplexer_11_out), .out(multiplexer_26_out), .sel(amount[1]));
  Multiplexer #(.enable("false")) multiplexer_27 (
    .in0(multiplexer_10_out), .in1(multiplexer_12_out), .out(multiplexer_27_out), .sel(amount[1]));
  Multiplexer #(.enable("false")) multiplexer_28 (
    .in0(multiplexer_18_out), .in1(multiplexer_22_out), .out(out[1]), .sel(amount[2]));
  Multiplexer #(.enable("false")) multiplexer_29 (
    .in0(multiplexer_19_out), .in1(multiplexer_23_out), .out(out[2]), .sel(amount[2]));
  Multiplexer #(.enable("false")) multiplexer_30 (
    .in0(multiplexer_11_out), .in1(multiplexer_13_out), .out(multiplexer_30_out), .sel(amount[1]));
  Multiplexer #(.enable("false")) multiplexer_31 (
    .in0(multiplexer_20_out), .in1(multiplexer_24_out), .out(out[3]), .sel(amount[2]));
  Multiplexer #(.enable("false")) multiplexer_32 (
    .in0(multiplexer_21_out), .in1(multiplexer_26_out), .out(out[4]), .sel(amount[2]));
  Multiplexer #(.enable("false")) multiplexer_33 (
    .in0(multiplexer_22_out), .in1(multiplexer_27_out), .out(out[5]), .sel(amount[2]));
  Multiplexer #(.enable("false")) multiplexer_34 (
    .in0(multiplexer_12_out), .in1(multiplexer_14_out), .out(multiplexer_34_out), .sel(amount[1]));
  Multiplexer #(.enable("false")) multiplexer_35 (
    .in0(multiplexer_13_out), .in1(multiplexer_15_out), .out(multiplexer_35_out), .sel(amount[1]));
  Multiplexer #(.enable("false")) multiplexer_36 (
    .in0(multiplexer_23_out), .in1(multiplexer_30_out), .out(out[6]), .sel(amount[2]));
  Multiplexer #(.enable("false")) multiplexer_37 (
    .in0(multiplexer_24_out), .in1(multiplexer_34_out), .out(out[7]), .sel(amount[2]));
  Multiplexer #(.enable("false")) multiplexer_38 (
    .in0(multiplexer_26_out), .in1(multiplexer_35_out), .out(out[8]), .sel(amount[2]));
  Multiplexer #(.enable("false")) multiplexer_39 (
    .in0(multiplexer_14_out), .in1(multiplexer_16_out), .out(multiplexer_39_out), .sel(amount[1]));
  Multiplexer #(.enable("false")) multiplexer_40 (
    .in0(multiplexer_15_out), .in1(\input [15]), .out(multiplexer_40_out), .sel(amount[1]));
  Multiplexer #(.enable("false")) multiplexer_41 (
    .in0(multiplexer_27_out), .in1(multiplexer_39_out), .out(out[9]), .sel(amount[2]));
  Multiplexer #(.enable("false")) multiplexer_42 (
    .in0(multiplexer_30_out), .in1(multiplexer_40_out), .out(out[10]), .sel(amount[2]));
  Multiplexer #(.enable("false")) multiplexer_43 (
    .in0(multiplexer_16_out), .in1(\input [15]), .out(multiplexer_43_out), .sel(amount[1]));
  Multiplexer #(.enable("false")) multiplexer_44 (
    .in0(multiplexer_34_out), .in1(multiplexer_43_out), .out(out[11]), .sel(amount[2]));
  Multiplexer #(.enable("false")) multiplexer_45 (
    .in0(multiplexer_35_out), .in1(\input [15]), .out(out[12]), .sel(amount[2]));
  Multiplexer #(.enable("false")) multiplexer_46 (
    .in0(multiplexer_39_out), .in1(\input [15]), .out(out[13]), .sel(amount[2]));
  Multiplexer #(.enable("false")) multiplexer_47 (
    .in0(multiplexer_40_out), .in1(\input [15]), .out(out[14]), .sel(amount[2]));
  Multiplexer #(.enable("false")) multiplexer_48 (
    .in0(multiplexer_43_out), .in1(\input [15]), .out(out[15]), .sel(amount[2]));

  // Other names for the same wires on the sheet: a0 = amount[0]; a1 = amount[1]; a2 = amount[2]

  // Notes on the sheet:
  //   0
  //   3
  //   13
  //   14
  //   15
  //   1
  //   8
  //   9
  //   10
  //   11
  //   12
  //   2
  //   7
  //   4
  //   6
  //   5
  //   15th bit
  //   out15
  //   out14
endmodule

module insnSplitter (
  input  [15:0] insn,
  output [3:0] opcode,
  output [5:0] immediate,
  output [2:0] Shamt,
  output [2:0] Rd,
  output [2:0] Rt,
  output [2:0] Rs,
  output [11:0] address
);


  assign address = insn[11:0];
  assign immediate = insn[5:0];
  assign opcode = insn[15:12];
  assign Rd = insn[5:3];
  assign Rs = insn[11:9];
  assign Rt = insn[8:6];
  assign Shamt = insn[2:0];
endmodule

module controlBox (
  input  [3:0] opcode,
  output dataWE,
  output RfWe,
  output isLoad,
  output useImmediate,
  output ALU2,
  output ALU1,
  output ALU0,
  output isBranch,
  output isJump,
  output isJal,
  output isJr,
  output readInput,
  output printOutput
);

  wire add, addi, beq, blt, j, \not , not_1_out, not_2_out, not_3_out, not_4_out, not_5_out, not_6_out,
       not_8_out, not_9_out, not_10_out, not_11_out, not_12_out, not_13_out, not_14_out, not_15_out,
       not_16_out, not_17_out, not_18_out, not_19_out, not_20_out, not_21_out, not_22_out, not_23_out,
       not_24_out, not_25_out, not_26_out, not_27_out, not_28_out, not_29_out, not_30_out, not_31_out,
       not_32_out, not_33_out, shl, shra, sub, \xor ;

  not not_1 (not_1_out, opcode[3]);
  and add0111 (add, opcode[0], opcode[1], opcode[2], not_1_out);
  not not_2 (not_2_out, opcode[0]);
  not not_3 (not_3_out, opcode[1]);
  not not_4 (not_4_out, opcode[2]);
  and sub1000 (sub, not_2_out, not_3_out, not_4_out, opcode[3]);
  not not_5 (not_5_out, opcode[0]);
  not not_6 (not_6_out, opcode[1]);
  and not_7 (\not , not_5_out, not_6_out, opcode[2], not_8_out);
  not not_8 (not_8_out, opcode[3]);
  not not_9 (not_9_out, opcode[1]);
  and u_xor (\xor , opcode[0], not_9_out, opcode[2], not_10_out);
  not not_10 (not_10_out, opcode[3]);
  not not_11 (not_11_out, opcode[0]);
  and u_addi (addi, not_11_out, opcode[1], opcode[2], not_12_out);
  not not_12 (not_12_out, opcode[3]);
  not not_13 (not_13_out, opcode[0]);
  not not_14 (not_14_out, opcode[1]);
  not not_15 (not_15_out, opcode[2]);
  not not_16 (not_16_out, opcode[3]);
  not not_17 (not_17_out, opcode[0]);
  not not_18 (not_18_out, opcode[2]);
  not not_19 (not_19_out, opcode[3]);
  not not_20 (not_20_out, opcode[2]);
  not not_21 (not_21_out, opcode[3]);
  and lw (isLoad, not_13_out, not_14_out, not_15_out, not_16_out);
  and u_beq (beq, not_17_out, opcode[1], not_18_out, not_19_out);
  and u_blt (blt, opcode[0], opcode[1], not_20_out, not_21_out);
  not not_22 (not_22_out, opcode[1]);
  or or_1 (RfWe, \xor , isJal, shl, add, sub, addi, \not , isLoad, shra, readInput);
  and jr (isJr, opcode[0], not_22_out, opcode[2], opcode[3]);
  not not_23 (not_23_out, opcode[0]);
  not not_24 (not_24_out, opcode[2]);
  not not_25 (not_25_out, opcode[1]);
  not not_26 (not_26_out, opcode[2]);
  not not_27 (not_27_out, opcode[3]);
  not not_28 (not_28_out, opcode[1]);
  not not_29 (not_29_out, opcode[2]);
  not not_30 (not_30_out, opcode[2]);
  and \input  (readInput, opcode[0], opcode[1], opcode[2], opcode[3]);
  and u_shl (shl, not_23_out, opcode[1], not_24_out, opcode[3]);
  and sw (dataWE, opcode[0], not_25_out, not_26_out, not_27_out);
  and u_shra (shra, opcode[0], not_28_out, not_29_out, opcode[3]);
  and u_j (j, opcode[0], opcode[1], not_30_out, opcode[3]);
  not not_31 (not_31_out, opcode[0]);
  not not_32 (not_32_out, opcode[1]);
  and jal (isJal, not_31_out, not_32_out, opcode[2], opcode[3]);
  not not_33 (not_33_out, opcode[0]);
  and \output  (printOutput, not_33_out, opcode[1], opcode[2], opcode[3]);
  or or_2 (useImmediate, isLoad, addi, shra, dataWE, shl);
  or or_3 (ALU2, shra, shl);
  or or_4 (ALU1, \not , \xor );
  or or_5 (ALU0, \xor , sub, blt, beq, shra);
  or or_6 (isBranch, beq, blt);
  or or_7 (isJump, j, isJal);

  // Other names for the same wires on the sheet: input = readInput; jal = isJal; jr = isJr; lw = isLoad;
  //   _0 = opcode[0]; _1 = opcode[1]; _2 = opcode[2]; _3 = opcode[3]; output = printOutput; sw = dataWE

  // Notes on the sheet:
  //   1
  //   0
  //   2
  //   3
endmodule

module RIJ (
  input  [3:0] opcode,
  output isR,
  output isI,
  output isJ
);

  wire addi_out, beq_out, blt_out, j_out, jal_out, lw_out, not_1_out, not_2_out, not_3_out, not_4_out,
       not_5_out, not_6_out, not_7_out, not_8_out, not_9_out, not_10_out, not_11_out, not_12_out, not_13_out,
       not_14_out, not_15_out, not_16_out, sw_out;

  not not_1 (not_1_out, opcode[0]);
  not not_2 (not_2_out, opcode[1]);
  not not_3 (not_3_out, opcode[2]);
  not not_4 (not_4_out, opcode[3]);
  not not_5 (not_5_out, opcode[2]);
  not not_6 (not_6_out, opcode[0]);
  not not_7 (not_7_out, opcode[1]);
  and lw (lw_out, not_1_out, not_2_out, not_3_out, not_4_out);
  not not_8 (not_8_out, opcode[1]);
  not not_9 (not_9_out, opcode[2]);
  not not_10 (not_10_out, opcode[3]);
  not not_11 (not_11_out, opcode[2]);
  not not_12 (not_12_out, opcode[3]);
  and sw (sw_out, opcode[0], not_8_out, not_9_out, not_10_out);
  not not_13 (not_13_out, opcode[0]);
  not not_14 (not_14_out, opcode[3]);
  and j (j_out, opcode[0], opcode[1], not_5_out, opcode[3]);
  and jal (jal_out, not_6_out, not_7_out, opcode[2], opcode[3]);
  and beq (beq_out, not_1_out, opcode[1], not_9_out, not_10_out);
  and blt (blt_out, opcode[0], opcode[1], not_11_out, not_12_out);
  and addi (addi_out, not_13_out, opcode[1], opcode[2], not_14_out);
  or or_1 (isJ, j_out, jal_out);
  or or_2 (isI, lw_out, sw_out, beq_out, blt_out, addi_out);
  not not_15 (not_15_out, isJ);
  not not_16 (not_16_out, isI);
  and and_1 (isR, not_16_out, not_15_out);

  // Notes on the sheet:
  //   0
  //   1
  //   2
  //   3
endmodule

module brancher (
  input  [15:0] ALUresult,
  input  [3:0] opcode,
  output doBranch
);

  wire beq_2_out, beq_out, blt_2_out, blt_out, iszero_1_out, not_1_out, not_2_out, not_3_out, not_4_out,
       not_5_out;

  isZero iszero_1 (.\input (ALUresult), .out(iszero_1_out));
  not not_1 (not_1_out, opcode[2]);
  not not_2 (not_2_out, opcode[3]);
  not not_3 (not_3_out, opcode[0]);
  not not_4 (not_4_out, opcode[2]);
  not not_5 (not_5_out, opcode[3]);
  and blt (blt_out, ALUresult[15], blt_2_out);
  and blt_2 (blt_2_out, opcode[0], opcode[1], not_1_out, not_2_out);
  and beq (beq_out, not_3_out, opcode[1], not_4_out, not_5_out);
  and beq_2 (beq_2_out, iszero_1_out, beq_out);
  or or_1 (doBranch, blt_out, beq_2_out);

  // Other names for the same wires on the sheet: _0 = opcode[0]; _1 = opcode[1]; _2 = opcode[2]; _3 = opcode[3]
endmodule
